// Logisim project Cofre.circ as structural Verilog
module Registrador_de_Estado (
  input  CLK,
  input  N3,
  input  N2,
  input  N1,
  input  N0,
  output S3,
  output S2,
  output S1,
  output S0
);

  D_Flip_Flop d_ff_1 (.clk(CLK), .D(N3), .Q(S3));  // open: Qn, preset, en, reset
  D_Flip_Flop d_ff_2 (.clk(CLK), .D(N2), .Q(S2));  // open: Qn, preset, en, reset
  D_Flip_Flop d_ff_3 (.clk(CLK), .D(N1), .Q(S1));  // open: Qn, preset, en, reset
  D_Flip_Flop d_ff_4 (.clk(CLK), .D(N0), .Q(S0));  // open: Qn, preset, en, reset
endmodule

module LogTeste (
  input  in_1,
  input  in_2,
  input  in_3,
  input  in_4,
  input  in_5,
  input  in_6,
  input  in_7,
  input  in_8,
  output out_9,
  output out_10,
  output out_11,
  output out_12,
  output out_13,
  output out_14,
  output out_15,
  output out_16,
  output out_17
);


  // Other names for the same wires on the sheet: A0 = in_8; A1 = in_7; A2 = in_6; A3 = in_5; ADD = in_2; B = out_15;
  //   B0 = out_12; B1 = out_11; B2 = out_10; B3 = out_9; G = out_14; ON = in_1; OUT = out_16; R = out_13; S = in_4;
  //   T = in_3; TELA = out_17
endmodule
