// Logisim project MDE.circ as structural Verilog
module \LÓGICA_COMBINACIONAL  (
  input  U,
  input  Y,
  input  S2,
  input  S1,
  input  S0
);
endmodule

module REGISTRADOR_DE_ESTADO (
  input  CLK,
  input  N2,
  input  N1,
  input  N0,
  output S2,
  output S1,
  output S0
);

  D_Flip_Flop d_ff_1 (.clk(CLK), .D(N2), .Q(S2));  // open: Qn, preset, en, reset
  D_Flip_Flop d_ff_2 (.clk(CLK), .D(N1), .Q(S1));  // open: Qn, preset, en, reset
  D_Flip_Flop d_ff_3 (.clk(CLK), .D(N0), .Q(S0));  // open: Qn, preset, en, reset
endmodule
