// Logisim project Memoria.circ as structural Verilog
module _1_bit (
  input  CLK,
  input  D,
  input  LER,
  input  EN,
  input  CLR,
  output Saida
);

  wire d_ff_1_q;

  D_Flip_Flop d_ff_1 (.clk(CLK), .D(D), .Q(d_ff_1_q), .en(EN), .reset(CLR));  // open: Qn, preset
  Multiplexer #(.enable("false")) multiplexer_1 (.in1(d_ff_1_q), .out(Saida), .sel(LER));  // open: in0
endmodule

module _13_bits (
  input  CLK,
  input  wd_en,
  input  CLR,
  input  rd_en,
  input  [12:0] wd_data,
  output [12:0] SAIDA
);

  _1_bit u_1_bit_1 (.CLK(CLK), .D(wd_data[0]), .EN(wd_en), .CLR(CLR), .Saida(SAIDA[0]), .LER(rd_en));
  _1_bit u_1_bit_2 (.CLK(CLK), .D(wd_data[1]), .EN(wd_en), .CLR(CLR), .Saida(SAIDA[1]), .LER(rd_en));
  _1_bit u_1_bit_3 (.CLK(CLK), .D(wd_data[2]), .EN(wd_en), .CLR(CLR), .Saida(SAIDA[2]), .LER(rd_en));
  _1_bit u_1_bit_4 (.CLK(CLK), .D(wd_data[3]), .EN(wd_en), .CLR(CLR), .Saida(SAIDA[3]), .LER(rd_en));
  _1_bit u_1_bit_5 (.CLK(CLK), .D(wd_data[4]), .EN(wd_en), .CLR(CLR), .Saida(SAIDA[4]), .LER(rd_en));
  _1_bit u_1_bit_6 (.CLK(CLK), .D(wd_data[5]), .EN(wd_en), .CLR(CLR), .Saida(SAIDA[5]), .LER(rd_en));
  _1_bit u_1_bit_7 (.CLK(CLK), .D(wd_data[6]), .EN(wd_en), .CLR(CLR), .Saida(SAIDA[6]), .LER(rd_en));
  _1_bit u_1_bit_8 (.CLK(CLK), .D(wd_data[7]), .EN(wd_en), .CLR(CLR), .Saida(SAIDA[7]), .LER(rd_en));
  _1_bit u_1_bit_9 (.CLK(CLK), .D(wd_data[8]), .EN(wd_en), .CLR(CLR), .Saida(SAIDA[8]), .LER(rd_en));
  _1_bit u_1_bit_10 (.CLK(CLK), .D(wd_data[9]), .EN(wd_en), .CLR(CLR), .Saida(SAIDA[9]), .LER(rd_en));
  _1_bit u_1_bit_11 (.CLK(CLK), .D(wd_data[10]), .EN(wd_en), .CLR(CLR), .Saida(SAIDA[10]), .LER(rd_en));
  _1_bit u_1_bit_12 (.CLK(CLK), .D(wd_data[11]), .EN(wd_en), .CLR(CLR), .Saida(SAIDA[11]), .LER(rd_en));
  _1_bit u_1_bit_13 (.CLK(CLK), .D(wd_data[12]), .EN(wd_en), .CLR(CLR), .Saida(SAIDA[12]), .LER(rd_en));

  // Other names for the same wires on the sheet: I0 = wd_data[0]; I1 = wd_data[1]; I2 = wd_data[2]; I3 = wd_data[3];
  //   I4 = wd_data[4]; I5 = wd_data[5]; I6 = wd_data[6]; I7 = wd_data[7]; I8 = wd_data[8]; I9 = wd_data[9];
  //   I10 = wd_data[10]; I11 = wd_data[11]; I12 = wd_data[12]
endmodule

module Conjunto_4Palavras (
  input  CLK,
  input  CLR,
  input  wd_addr_01,
  input  wd_addr_02,
  input  wd_addr_03,
  input  wd_addr_04,
  input  rd_addr_01,
  input  rd_addr_02,
  input  rd_addr_03,
  input  rd_addr_04,
  input  [12:0] wd_data,
  output [12:0] rd_data,
  output [12:0] rd_data_2,
  output [12:0] rd_data_3,
  output [12:0] rd_data_4
);

  _13_bits u_13_bits_1 (
    .CLK(CLK), .wd_en(wd_addr_01), .CLR(CLR), .rd_en(rd_addr_01), .SAIDA(rd_data), .wd_data(wd_data));
  _13_bits u_13_bits_2 (
    .CLK(CLK), .wd_en(wd_addr_02), .CLR(CLR), .rd_en(rd_addr_02), .SAIDA(rd_data_2), .wd_data(wd_data));
  _13_bits u_13_bits_3 (
    .CLK(CLK), .wd_en(wd_addr_03), .CLR(CLR), .rd_en(rd_addr_03), .SAIDA(rd_data_3), .wd_data(wd_data));
  _13_bits u_13_bits_4 (
    .CLK(CLK), .wd_en(wd_addr_04), .CLR(CLR), .rd_en(rd_addr_04), .SAIDA(rd_data_4), .wd_data(wd_data));
endmodule

module Circuito_Memoria (
  input  [12:0] w_data,
  input  CLK,
  input  CLR,
  input  wd,
  input  rd,
  input  [3:0] wd_addr,
  input  [3:0] rd_addr,
  output [12:0] rd_data
);

  wire r0, r1, r2, r3, r4, r5, r6, r7, r8, r9, r10, r11, r12, r13, r14, r15, w0, w1, w2, w3, w4, w5, w6, w7,
       w8, w9, w10, w11, w12, w13, w14, w15;

  Decoder #(.select(4)) decoder_1 (
    .out0(w0), .out1(w1), .out2(w2), .out3(w3), .out4(w4), .out5(w5), .out6(w6), .out7(w7), .out8(w8),
    .out9(w9), .out10(w10), .out11(w11), .out12(w12), .out13(w13), .out14(w14), .out15(w15), .sel(wd_addr),
    .en(wd));
  Conjunto_4Palavras conjunto_4palavras_1 (
    .CLK(CLK), .wd_data(w_data), .rd_data(rd_data), .rd_data_2(rd_data), .rd_data_3(rd_data),
    .rd_data_4(rd_data), .wd_addr_01(w0), .wd_addr_02(w1), .wd_addr_03(w2), .wd_addr_04(w3), .rd_addr_01(r0),
    .rd_addr_02(r1), .rd_addr_03(r2), .rd_addr_04(r3), .CLR(CLR));
  Conjunto_4Palavras conjunto_4palavras_2 (
    .CLK(CLK), .wd_data(w_data), .rd_data(rd_data), .rd_data_2(rd_data), .rd_data_3(rd_data),
    .rd_data_4(rd_data), .wd_addr_01(w4), .wd_addr_02(w5), .wd_addr_03(w6), .wd_addr_04(w7), .rd_addr_01(r4),
    .rd_addr_02(r5), .rd_addr_03(r6), .rd_addr_04(r7), .CLR(CLR));
  Conjunto_4Palavras conjunto_4palavras_3 (
    .CLK(CLK), .wd_data(w_data), .rd_data(rd_data), .rd_data_2(rd_data), .rd_data_3(rd_data),
    .rd_data_4(rd_data), .wd_addr_01(w8), .wd_addr_02(w9), .wd_addr_03(w10), .wd_addr_04(w11),
    .rd_addr_01(r8), .rd_addr_02(r9), .rd_addr_03(r10), .rd_addr_04(r11), .CLR(CLR));
  Conjunto_4Palavras conjunto_4palavras_4 (
    .CLK(CLK), .wd_data(w_data), .rd_data(rd_data), .rd_data_2(rd_data), .rd_data_3(rd_data),
    .rd_data_4(rd_data), .wd_addr_01(w12), .wd_addr_02(w13), .wd_addr_03(w14), .wd_addr_04(w15),
    .rd_addr_01(r12), .rd_addr_02(r13), .rd_addr_03(r14), .rd_addr_04(r15), .CLR(CLR));
  Decoder #(.select(4)) decoder_2 (
    .out0(r0), .out1(r1), .out2(r2), .out3(r3), .out4(r4), .out5(r5), .out6(r6), .out7(r7), .out8(r8),
    .out9(r9), .out10(r10), .out11(r11), .out12(r12), .out13(r13), .out14(r14), .out15(r15), .sel(rd_addr),
    .en(rd));
endmodule
