// Logisim project Deslocador.circ as structural Verilog: 3 circuits, main circuit main
module main (
);

  Shifter shifter_1 ();  // open: E, Z, c, out_6, in_1, in_3
  Shifte shifte_1 ();  // open: E, Z, in_1, out_5, in_3
endmodule

module Shifter (
  input  [7:0] in_1,
  input  E,
  input  [2:0] in_3,
  output Z,
  output c,
  output [7:0] out_6
);

  wire multiplexer_1_out, multiplexer_2_out, multiplexer_4_out, multiplexer_5_out, multiplexer_7_out,
       multiplexer_8_out, multiplexer_10_out, multiplexer_11_out, multiplexer_13_out, multiplexer_14_out,
       multiplexer_16_out, multiplexer_17_out, multiplexer_19_out, multiplexer_20_out, multiplexer_22_out,
       multiplexer_23_out, or_1_out;

  Multiplexer multiplexer_1 (.in0(in_1[7]), .in1(in_1[6]), .out(multiplexer_1_out), .sel(in_3[0]), .en(E));
  Multiplexer multiplexer_2 (
    .in0(multiplexer_1_out), .in1(multiplexer_7_out), .out(multiplexer_2_out), .sel(in_3[1]), .en(E));
  Multiplexer multiplexer_3 (.in0(multiplexer_2_out), .in1(multiplexer_14_out), .out(c), .sel(in_3[2]), .en(E));
  Multiplexer multiplexer_4 (.in0(in_1[6]), .in1(in_1[5]), .out(multiplexer_4_out), .sel(in_3[0]), .en(E));
  Multiplexer multiplexer_5 (
    .in0(multiplexer_4_out), .in1(multiplexer_10_out), .out(multiplexer_5_out), .sel(in_3[1]), .en(E));
  Multiplexer multiplexer_6 (.in0(multiplexer_5_out), .in1(multiplexer_17_out), .out(out_6[6]), .sel(in_3[2]), .en(E));
  Multiplexer multiplexer_7 (.in0(in_1[5]), .in1(in_1[4]), .out(multiplexer_7_out), .sel(in_3[0]), .en(E));
  Multiplexer multiplexer_8 (
    .in0(multiplexer_7_out), .in1(multiplexer_13_out), .out(multiplexer_8_out), .sel(in_3[1]), .en(E));
  Multiplexer multiplexer_9 (.in0(multiplexer_8_out), .in1(multiplexer_20_out), .out(out_6[5]), .sel(in_3[2]), .en(E));
  Multiplexer multiplexer_10 (.in0(in_1[4]), .in1(in_1[3]), .out(multiplexer_10_out), .sel(in_3[0]), .en(E));
  Multiplexer multiplexer_11 (
    .in0(multiplexer_10_out), .in1(multiplexer_16_out), .out(multiplexer_11_out), .sel(in_3[1]), .en(E));
  Multiplexer multiplexer_12 (
    .in0(multiplexer_11_out), .in1(multiplexer_23_out), .out(out_6[4]), .sel(in_3[2]), .en(E));
  Multiplexer multiplexer_13 (.in0(in_1[3]), .in1(in_1[2]), .out(multiplexer_13_out), .sel(in_3[0]), .en(E));
  Multiplexer multiplexer_14 (
    .in0(multiplexer_13_out), .in1(multiplexer_19_out), .out(multiplexer_14_out), .sel(in_3[1]), .en(E));
  Multiplexer multiplexer_15 (.in0(multiplexer_14_out), .in1(1'b0), .out(out_6[3]), .sel(in_3[2]), .en(E));
  Multiplexer multiplexer_16 (.in0(in_1[2]), .in1(in_1[1]), .out(multiplexer_16_out), .sel(in_3[0]), .en(E));
  Multiplexer multiplexer_17 (
    .in0(multiplexer_16_out), .in1(multiplexer_22_out), .out(multiplexer_17_out), .sel(in_3[1]), .en(E));
  Multiplexer multiplexer_18 (.in0(multiplexer_17_out), .in1(1'b0), .out(out_6[2]), .sel(in_3[2]), .en(E));
  Multiplexer multiplexer_19 (.in0(in_1[1]), .in1(in_1[0]), .out(multiplexer_19_out), .sel(in_3[0]), .en(E));
  Multiplexer multiplexer_20 (.in0(multiplexer_19_out), .in1(1'b0), .out(multiplexer_20_out), .sel(in_3[1]), .en(E));
  Multiplexer multiplexer_21 (.in0(multiplexer_20_out), .in1(1'b0), .out(out_6[1]), .sel(in_3[2]), .en(E));
  Multiplexer multiplexer_22 (.in0(in_1[0]), .in1(1'b0), .out(multiplexer_22_out), .sel(in_3[0]), .en(E));
  Multiplexer multiplexer_23 (.in0(multiplexer_22_out), .in1(1'b0), .out(multiplexer_23_out), .sel(in_3[1]), .en(E));
  Multiplexer multiplexer_24 (.in0(multiplexer_23_out), .in1(1'b0), .out(out_6[0]), .sel(in_3[2]), .en(E));
  or or_1 (or_1_out, c, out_6[6], out_6[5], out_6[4], out_6[3], out_6[2], out_6[1], out_6[0]);
  not not_1 (Z, or_1_out);

  assign out_6[7] = c;

  // Other names for the same wires on the sheet: q0 = out_6[0]; q1 = out_6[1]; q2 = out_6[2]; q3 = out_6[3];
  //   q4 = out_6[4]; q5 = out_6[5]; q6 = out_6[6]; q7 = c

  // Notes on the sheet:
  //   s2
  //   s0
  //   s1
  //   I7
  //   I6
  //   I5
  //   I4
  //   I3
  //   I2
  //   I1
  //   I0
endmodule

module Shifte (
  input  [7:0] in_1,
  input  E,
  input  [2:0] in_3,
  output Z,
  output [7:0] out_5
);

  wire multiplexer_1_out, multiplexer_2_out, multiplexer_4_out, multiplexer_5_out, multiplexer_7_out,
       multiplexer_8_out, multiplexer_10_out, multiplexer_11_out, multiplexer_13_out, multiplexer_14_out,
       multiplexer_16_out, multiplexer_17_out, multiplexer_19_out, multiplexer_20_out, multiplexer_22_out,
       multiplexer_23_out, or_1_out;

  Multiplexer multiplexer_1 (.in0(in_1[7]), .in1(1'b0), .out(multiplexer_1_out), .sel(in_3[0]), .en(E));
  Multiplexer multiplexer_2 (.in0(multiplexer_1_out), .in1(1'b0), .out(multiplexer_2_out), .sel(in_3[1]), .en(E));
  Multiplexer multiplexer_3 (.in0(multiplexer_2_out), .in1(1'b0), .out(out_5[7]), .sel(in_3[2]), .en(E));
  Multiplexer multiplexer_4 (.in0(in_1[6]), .in1(in_1[7]), .out(multiplexer_4_out), .sel(in_3[0]), .en(E));
  Multiplexer multiplexer_5 (.in0(multiplexer_4_out), .in1(1'b0), .out(multiplexer_5_out), .sel(in_3[1]), .en(E));
  Multiplexer multiplexer_6 (.in0(multiplexer_5_out), .in1(1'b0), .out(out_5[6]), .sel(in_3[2]), .en(E));
  Multiplexer multiplexer_7 (.in0(in_1[5]), .in1(in_1[6]), .out(multiplexer_7_out), .sel(in_3[0]), .en(E));
  Multiplexer multiplexer_8 (
    .in0(multiplexer_7_out), .in1(multiplexer_1_out), .out(multiplexer_8_out), .sel(in_3[1]), .en(E));
  Multiplexer multiplexer_9 (.in0(multiplexer_8_out), .in1(1'b0), .out(out_5[5]), .sel(in_3[2]), .en(E));
  Multiplexer multiplexer_10 (.in0(in_1[4]), .in1(in_1[5]), .out(multiplexer_10_out), .sel(in_3[0]), .en(E));
  Multiplexer multiplexer_11 (
    .in0(multiplexer_10_out), .in1(multiplexer_4_out), .out(multiplexer_11_out), .sel(in_3[1]), .en(E));
  Multiplexer multiplexer_12 (.in0(multiplexer_11_out), .in1(1'b0), .out(out_5[4]), .sel(in_3[2]), .en(E));
  Multiplexer multiplexer_13 (.in0(in_1[3]), .in1(in_1[4]), .out(multiplexer_13_out), .sel(in_3[0]), .en(E));
  Multiplexer multiplexer_14 (
    .in0(multiplexer_13_out), .in1(multiplexer_7_out), .out(multiplexer_14_out), .sel(in_3[1]), .en(E));
  Multiplexer multiplexer_15 (.in0(multiplexer_14_out), .in1(multiplexer_2_out), .out(out_5[3]), .sel(in_3[2]), .en(E));
  Multiplexer multiplexer_16 (.in0(in_1[2]), .in1(in_1[3]), .out(multiplexer_16_out), .sel(in_3[0]), .en(E));
  Multiplexer multiplexer_17 (
    .in0(multiplexer_16_out), .in1(multiplexer_10_out), .out(multiplexer_17_out), .sel(in_3[1]), .en(E));
  Multiplexer multiplexer_18 (.in0(multiplexer_17_out), .in1(multiplexer_5_out), .out(out_5[2]), .sel(in_3[2]), .en(E));
  Multiplexer multiplexer_19 (.in0(in_1[1]), .in1(in_1[2]), .out(multiplexer_19_out), .sel(in_3[0]), .en(E));
  Multiplexer multiplexer_20 (
    .in0(multiplexer_19_out), .in1(multiplexer_13_out), .out(multiplexer_20_out), .sel(in_3[1]), .en(E));
  Multiplexer multiplexer_21 (.in0(multiplexer_20_out), .in1(multiplexer_8_out), .out(out_5[1]), .sel(in_3[2]), .en(E));
  Multiplexer multiplexer_22 (.in0(in_1[0]), .in1(in_1[1]), .out(multiplexer_22_out), .sel(in_3[0]), .en(E));
  Multiplexer multiplexer_23 (
    .in0(multiplexer_22_out), .in1(multiplexer_16_out), .out(multiplexer_23_out), .sel(in_3[1]), .en(E));
  Multiplexer multiplexer_24 (
    .in0(multiplexer_23_out), .in1(multiplexer_11_out), .out(out_5[0]), .sel(in_3[2]), .en(E));
  or or_1 (or_1_out, out_5[7], out_5[6], out_5[5], out_5[4], out_5[3], out_5[2], out_5[1], out_5[0]);
  not not_1 (Z, or_1_out);

  // Other names for the same wires on the sheet: q0 = out_5[0]; q1 = out_5[1]; q2 = out_5[2]; q3 = out_5[3];
  //   q4 = out_5[4]; q5 = out_5[5]; q6 = out_5[6]; q7 = out_5[7]

  // Notes on the sheet:
  //   s0
  //   s2
  //   s1
  //   I7
  //   I6
  //   I5
  //   I4
  //   I3
  //   I2
  //   I1
  //   I0
endmodule
