// Logisim project Multiplicador.circ as structural Verilog
module Multiplicador_8bits (
  input  in_1,
  input  in_2,
  input  in_3,
  input  in_4,
  input  in_5,
  input  in_6,
  input  in_7,
  input  in_8,
  input  in_9,
  input  in_10,
  input  in_11,
  input  in_12,
  input  in_13,
  input  in_14,
  input  in_15,
  input  in_16,
  input  Cin,
  output [15:0] out_18,
  output out_19
);

  wire add16_1_out_5, add16_2_out_5, add16_3_out_5, add16_4_out_5, add16_5_out_5, add16_6_out_5;
  wire [15:0] add16_1_out_4, add16_2_out_4, add16_3_out_4, add16_4_out_4, add16_5_out_4, add16_6_out_4, m0,
       m1;
  wire [15:1] m2;
  wire [15:2] m3;
  wire [15:3] m4;
  wire [15:4] m5;
  wire [15:5] m6;
  wire [15:6] m7;

  ADD16 add16_1 (
    .in_2(Cin), .in_1({{8{m0[15]}}, m0[7:0]}), .in_3({{7{m1[15]}}, m1[8:0]}), .out_4(add16_1_out_4),
    .out_5(add16_1_out_5));
  ADD16 add16_2 (
    .in_2(add16_1_out_5), .in_1(add16_1_out_4), .in_3({{6{m2[15]}}, m2[9:1], m2[1]}), .out_4(add16_2_out_4),
    .out_5(add16_2_out_5));
  ADD16 add16_3 (
    .in_2(add16_2_out_5), .in_1(add16_2_out_4), .in_3({{5{m3[15]}}, m3[10:2], {2{m3[2]}}}),
    .out_4(add16_3_out_4), .out_5(add16_3_out_5));
  ADD16 add16_4 (
    .in_2(add16_3_out_5), .in_1(add16_3_out_4), .in_3({{4{m4[15]}}, m4[11:3], {3{m4[3]}}}),
    .out_4(add16_4_out_4), .out_5(add16_4_out_5));
  ADD16 add16_5 (
    .in_2(add16_4_out_5), .in_1(add16_4_out_4), .in_3({{3{m5[15]}}, m5[12:4], {4{m5[4]}}}),
    .out_4(add16_5_out_4), .out_5(add16_5_out_5));
  ADD16 add16_6 (
    .in_2(add16_5_out_5), .in_1(add16_5_out_4), .in_3({{2{m6[15]}}, m6[13:5], {5{m6[5]}}}),
    .out_4(add16_6_out_4), .out_5(add16_6_out_5));
  ADD16 add16_7 (.in_2(add16_6_out_5), .in_1(add16_6_out_4), .in_3({m7, {6{m7[6]}}}), .out_4(out_18), .out_5(out_19));
  and and_1 (m0[7], in_1, in_16);
  and and_2 (m1[8], in_1, in_15);
  and and_3 (m2[9], in_1, in_14);
  and and_4 (m3[10], in_1, in_13);
  and and_5 (m4[11], in_1, in_12);
  and and_6 (m0[6], in_2, in_16);
  and and_7 (m1[7], in_2, in_15);
  and and_8 (m2[8], in_2, in_14);
  Pull_Resistor pull_resistor_1 (.node(m2[15]));
  and and_9 (m3[9], in_2, in_13);
  and and_10 (m4[10], in_2, in_12);
  Pull_Resistor pull_resistor_2 (.node(m4[15]));
  and and_11 (m0[5], in_3, in_16);
  Pull_Resistor pull_resistor_3 (.node(m0[15]));
  and and_12 (m1[6], in_3, in_15);
  Pull_Resistor pull_resistor_4 (.node(m1[15]));
  and and_13 (m2[7], in_3, in_14);
  and and_14 (m3[8], in_3, in_13);
  Pull_Resistor pull_resistor_5 (.node(m3[15]));
  and and_15 (m4[9], in_3, in_12);
  and and_16 (m0[4], in_4, in_16);
  and and_17 (m1[5], in_4, in_15);
  and and_18 (m2[6], in_4, in_14);
  and and_19 (m3[7], in_4, in_13);
  and and_20 (m4[8], in_4, in_12);
  and and_21 (m0[3], in_5, in_16);
  and and_22 (m1[4], in_5, in_15);
  Pull_Resistor pull_resistor_6 (.node(m1[0]));
  and and_23 (m2[5], in_5, in_14);
  Pull_Resistor pull_resistor_7 (.node(m2[1]));
  and and_24 (m3[6], in_5, in_13);
  Pull_Resistor pull_resistor_8 (.node(m3[2]));
  and and_25 (m4[7], in_5, in_12);
  Pull_Resistor pull_resistor_9 (.node(m4[3]));
  and and_26 (m0[2], in_6, in_16);
  and and_27 (m1[3], in_6, in_15);
  and and_28 (m2[4], in_6, in_14);
  and and_29 (m3[5], in_6, in_13);
  and and_30 (m4[6], in_6, in_12);
  and and_31 (m0[1], in_7, in_16);
  and and_32 (m1[2], in_7, in_15);
  and and_33 (m2[3], in_7, in_14);
  and and_34 (m4[5], in_7, in_12);
  and and_35 (m0[0], in_8, in_16);
  and and_36 (m1[1], in_8, in_15);
  and and_37 (m2[2], in_8, in_14);
  and and_38 (m3[4], in_7, in_13);
  and and_39 (m3[3], in_8, in_13);
  and and_40 (m4[4], in_8, in_12);
  and and_41 (m5[12], in_1, in_11);
  and and_42 (m6[13], in_1, in_10);
  and and_43 (m7[14], in_1, in_9);
  and and_44 (m5[11], in_2, in_11);
  and and_45 (m6[12], in_2, in_10);
  and and_46 (m7[13], in_2, in_9);
  and and_47 (m5[10], in_3, in_11);
  Pull_Resistor pull_resistor_10 (.node(m5[15]));
  and and_48 (m6[11], in_3, in_10);
  Pull_Resistor pull_resistor_11 (.node(m6[15]));
  and and_49 (m7[12], in_3, in_9);
  Pull_Resistor pull_resistor_12 (.node(m7[15]));
  and and_50 (m5[9], in_4, in_11);
  and and_51 (m6[10], in_4, in_10);
  and and_52 (m7[11], in_4, in_9);
  and and_53 (m5[8], in_5, in_11);
  and and_54 (m6[9], in_5, in_10);
  Pull_Resistor pull_resistor_13 (.node(m6[5]));
  and and_55 (m7[10], in_5, in_9);
  and and_56 (m5[7], in_6, in_11);
  Pull_Resistor pull_resistor_14 (.node(m5[4]));
  and and_57 (m6[8], in_6, in_10);
  Pull_Resistor pull_resistor_15 (.node(m7[6]));
  and and_58 (m7[9], in_6, in_9);
  and and_59 (m5[6], in_7, in_11);
  and and_60 (m6[7], in_7, in_10);
  and and_61 (m7[8], in_7, in_9);
  and and_62 (m5[5], in_8, in_11);
  and and_63 (m6[6], in_8, in_10);
  and and_64 (m7[7], in_8, in_9);

  // Other names for the same wires on the sheet: a0 = in_8; a1 = in_7; a2 = in_6; a3 = in_5; a4 = in_4; a5 = in_3;
  //   a6 = in_2; a7 = in_1; b0 = in_16; b1 = in_15; b2 = in_14; b3 = in_13; b4 = in_12; b5 = in_11; b6 = in_10;
  //   b7 = in_9; m0[14:8] = {7{m0[15]}}; m1[14:9] = {6{m1[15]}}; m2 (some bits) = {{5{m2[15]}}, m2[1]};
  //   m3 (some bits) = {{4{m3[15]}}, {2{m3[2]}}}; m4 (some bits) = {{3{m4[15]}}, {3{m4[3]}}};
  //   m5 (some bits) = {{2{m5[15]}}, {4{m5[4]}}}; m6 (some bits) = {m6[15], {5{m6[5]}}}; m7[5:0] = {6{m7[6]}}

  // Notes on the sheet:
  //   Cout
endmodule

module Multiplicador_4bits (
  input  [3:0] in_1
);
endmodule
