// Logisim project ULA.circ as structural Verilog
module main (
);

  // ADD8 add8_1: pin names not known
  // SUB8 sub8_1: pin names not known
  // Multiplicador_8bits multiplicador_8bits_1: pin names not known
  // AND and_1: pin names not known
  // OR or_1: pin names not known
  // XOR xor_1: pin names not known
  // NOT not_1: pin names not known
  // Shifter shifter_1: pin names not known
  // Shifte shifte_1: pin names not known
endmodule
