// Logisim project Somador_BCD.circ as structural Verilog
module Somador_BCD_Unidades (
  input  A0,
  input  B0,
  input  Cin_usuario,
  input  A1,
  input  B1,
  input  A2,
  input  B2,
  input  A3,
  input  B3,
  input  A4,
  input  B4,
  input  A5,
  input  B5,
  input  A6,
  input  B6,
  input  A7,
  input  B7,
  output A,
  output B,
  output C,
  output D,
  output A_2,
  output B_2,
  output C_2,
  output D_2,
  output C_OUT
);

  wire and_1_out, and_2_out, and_3_out, and_4_out, and_5_out, and_6_out, and_7_out, and_8_out, CARRY_P_DEZ,
       EN, somador_completo_1_co, somador_completo_2_co, somador_completo_3_co, somador_completo_5_co,
       somador_completo_6_co, somador_completo_7_co, U0, U1, U2, U3, US0, US1, US2, US3;

  Somador_Completo somador_completo_1 (.A(A0), .B(B0), .cin(Cin_usuario), .co(somador_completo_1_co), .s(U0));
  Somador_Completo somador_completo_2 (.A(A1), .B(B1), .cin(somador_completo_1_co), .co(somador_completo_2_co), .s(U1));
  Somador_Completo somador_completo_3 (.A(A2), .B(B2), .cin(somador_completo_2_co), .co(somador_completo_3_co), .s(U2));
  Somador_Completo somador_completo_4 (.A(A3), .B(B3), .cin(somador_completo_3_co), .s(U3));  // open: co
  Somador_Completo somador_completo_5 (.A(A4), .B(B4), .cin(CARRY_P_DEZ), .co(somador_completo_5_co), .s(A_2));
  Somador_Completo somador_completo_6 (
    .A(A5), .B(B5), .cin(somador_completo_5_co), .co(somador_completo_6_co), .s(B_2));
  Somador_Completo somador_completo_7 (
    .A(A6), .B(B6), .cin(somador_completo_6_co), .co(somador_completo_7_co), .s(C_2));
  Somador_Completo somador_completo_8 (.A(A7), .B(B7), .cin(somador_completo_7_co), .co(C_OUT), .s(D_2));
  comparador_de_mag comparador_de_mag_1 (
    .A0(U0), .B0(1'b1), .A1(U1), .B1(1'b0), .A2(U2), .B2(1'b0), .A3(U3), .B3(1'b1), .out_11(EN));  // open: out_9, out_10
  and and_1 (and_1_out, US0, EN);
  and and_2 (and_2_out, US1, EN);
  and and_3 (and_3_out, US2, EN);
  and and_4 (and_4_out, US3, EN);
  and and_5 (and_5_out, U0, ~EN);  // AND_Gate
  and and_6 (and_6_out, U1, ~EN);  // AND_Gate
  and and_7 (and_7_out, U2, ~EN);  // AND_Gate
  and and_8 (and_8_out, U3, ~EN);  // AND_Gate
  or or_1 (A, and_1_out, and_5_out);
  or or_2 (B, and_2_out, and_6_out);
  or or_3 (C, and_3_out, and_7_out);
  or or_4 (D, and_4_out, and_8_out);
  somador_4bits somador_4bits_1 (
    .out_11(US1), .out_12(US2), .MSB_3(US3), .MSB(1'b0), .in_2(1'b1), .LSB(1'b1), .in_4(1'b0), .MSB_2(U3),
    .in_6(U2), .LSB_2(U1), .in_8(U0), .LSB_3(US0), .in_9(EN), .out_14(CARRY_P_DEZ));

  // Notes on the sheet:
  //   SOMADOR PARA UNIDADES
  //   SOMADOR PARA DEZENAS
  //   LÓGICA PARA SOMAR 6
endmodule

module Meio_somador (
  input  A,
  input  B,
  output co,
  output s
);

  and and_1 (co, A, B);
  xor xor_1 (s, B, A);
endmodule

module Somador_Completo (
  input  A,
  input  B,
  input  cin,
  output co,
  output s
);

  wire and_1_out, and_2_out, and_3_out, xor_1_out;

  and and_1 (and_1_out, A, B);
  and and_2 (and_2_out, A, cin);
  and and_3 (and_3_out, B, cin);
  xor xor_1 (xor_1_out, A, B);
  xor xor_2 (s, xor_1_out, cin);
  or or_1 (co, and_1_out, and_2_out, and_3_out);
endmodule
